# Fritzing sketch SynthVisor Schematic (saved by Fritzing 0.9.4)
circuit board: 8.46667cm x 5.64444cm
breadboards: 1

parts:
  Arduino = Arduino Uno (Rev3)
  HC-05 = Bluetooth HC-05 Macho
  R2 = Resistor [tolerance=±5% resistance=2k package=THT]
  R1 = Resistor [tolerance=±5% resistance=1k package=THT]

nets:
  GND: Arduino.GND, HC-05.GND, R2.Pin_1
  N1: Arduino.D0/RX, HC-05.RXD
  N2: Arduino.D1/TX, R1.Pin_0
  5V: Arduino.5V, HC-05.VCC
  N3: HC-05.TXD, R2.Pin_0, R1.Pin_1
